# Fritzing sketch Sketch_HW_v1 (saved by Fritzing 0.9.9b)
breadboards: 1

parts:
  CAMERA1 = TTL Serial JPEG Camera  # not connected
  M2 = DC Motor
  J1 = Basic Servo  # not connected
  J2 = Basic Servo  # not connected
  VCC3 = 4 x AAA Battery Mount
  Part1 = Adafruit PWM Servo Featherwing [part_number="Adafruit #2928"]  # not connected
  VCC2 = 4 x AAA Battery Mount
  Part2 = Adafruit TB6612 DC and Stepper Motor Driver [part_number="Adafruit #2448"]
  M1 = DC Motor
  VCC1 = 4 x AAA Battery Mount  # not connected
  Raspberry_Pi1 = Raspberry Pi B+

nets (from the breadboard view):
  N1: M2.pin_1, Part2.MOTORB1
  N2: M2.pin_2, Part2.MOTORB2
  GND: VCC3.-, Part2.GND, Raspberry_Pi1.GPIO14, Raspberry_Pi1.GND
  N3: VCC3.+, VCC2.-
  N4: Part2.BIN2, Raspberry_Pi1.GPIO27
  N5: Part2.BIN1, Raspberry_Pi1.GPIO3
  N6: Part2.AIN1, Raspberry_Pi1.GPIO9
  N7: Part2.AIN2, Raspberry_Pi1.GPIO11
  N8: Part2.MOTORA1, M1.pin_2
  N9: Part2.MOTORA2, M1.pin_1

custom parts:
  TTL Serial JPEG Camera: TTL Serial JPEG Camera with NTSC Out
  Adafruit PWM Servo Featherwing: This is the 8-Channel PWM or Servo​ FeatherWing, you can add 8 x 12-bit PWM outputs to your Feather board. You want to make a cool robot, maybe a hexapod walker, or maybe just a piece of art with a lot of moving parts. Or maybe you want to drive a lot of LEDs with precise PWM output. What now? You could give up OR you could just get our handy PWM and Servo FeatherWing. It's a lot like our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
  Adafruit TB6612 DC and Stepper Motor Driver: Spin two DC motors, step one bi-polar or uni-polar stepper, or fire off two solenoids with 1.2A per channel using the TB6612. These are perhaps better known as "the drivers in our assembled Adafruit Motorshield or Motor HAT." We really like these dual H-bridges, so if you want to control motors without a shield or HAT these are easy to include on any solderless breadboard or perma-proto.
